# Fritzing sketch debouncing (saved by Fritzing 0.9.3b)
breadboards: 1

parts:
  R1 = Resistor [tolerance=±5% resistance=10k package=THT]
  S1 = Pushbutton [package="[SMD]"]
  Part1 = Arduino Uno (Rev3)
  IC1 = IC, DIP package, 8 pins [chip_label=7404]
  C1 = Electrolytic Capacitor [capacitance=1µF package="100 mil [THT, electrolytic]"]

nets:
  N1: R1.Pin_0, Part1.5V, IC1.pin8
  N2: R1.Pin_1, S1.Pin_3, S1.Pin_4, IC1.pin7, C1.-
  N3: S1.Pin_1, S1.Pin_2, Part1.GND, IC1.pin4, C1.+
  N4: Part1.D2, IC1.pin6
